# Fritzing sketch board (saved by Fritzing 0.9.3b)
perfboards: 1

parts:
  U1 = 74HC04_HEX_INVERTER [package=dil14]
  IC3 = DIP - 14 pins [chip_label=74LS86 package="DIP (Dual Inline) [THT]"]
  IC6 = DIP - 16 pins [chip_label=74LS76 package="DIP (Dual Inline) [THT]"]
  IC7 = DIP - 16 pins [chip_label=74LS76 package="DIP (Dual Inline) [THT]"]
  IC8 = Voltage Regulator [package=78xxl]
  J1 = Screw terminal - 2 pins [package=THT]
  C1_0_33uF = Capacitor Polarized [package=cpol-radial-10uf-25v]
  C2_0_1uF = Capacitor Polarized [package=cpol-radial-10uf-25v]
  S1 = Momentary Switch [package=ksa_sealed_tac_switch]
  R1 = Resistor [tolerance=±5% resistance=10k package=THT]
  LED1 = LED - 5mm [color="Red (633nm)" package="5 mm [THT]"]
  LED2 = LED - 5mm [color="Red (633nm)" package="5 mm [THT]"]
  LED3 = LED - 5mm [color="Red (633nm)" package="5 mm [THT]"]
  LED4 = LED - 5mm [color="Red (633nm)" package="5 mm [THT]"]
  R2 = Resistor [tolerance=±5% resistance=220 package=THT]
  R3 = Resistor [tolerance=±5% resistance=220 package=THT]
  R4 = Resistor [tolerance=±5% resistance=220 package=THT]
  R5 = Resistor [tolerance=±5% resistance=220 package=THT]
  S2 = Toggle Switch [package=THT]
  U2 = 555 Timer [package="DIP8 [THT]"]
  R6 = Resistor [tolerance=±5% resistance=47k package=THT]
  C1 = Electrolytic Capacitor [capacitance=10µF package="100 mil [THT, electrolytic]"]
  C2 = Electrolytic Capacitor [capacitance=10nF package="100 mil [THT, electrolytic]"]
  R7 = Resistor [tolerance=±5% resistance=47k package=THT]
  S3 = Momentary Switch [package=ksa_sealed_tac_switch]
  S4 = Toggle Switch [package=THT]

nets:
  IN-C: U1.1A, IC3.Y4, IC6.1J
  !IN-C: U1.1Y, IC6.1K
  IN-D: U1.2A, IC3.V3, IC6.2J
  !IN-D: U1.2Y, IC6.2K
  GND: U1.GND, IC3.GND, IC6.GND, IC7.GND, IC8.GND, J1.pin1, C1_0_33uF.-, C2_0_1uF.-, S1.3, S1.4, R2.Pin_1, R3.Pin_1, R4.Pin_1, R5.Pin_1, U2.Ground, C1.-, C2.-, S3.3, S3.4, S4.L2
  !IN-B: U1.5Y, IC7.2K
  IN-B: U1.5A, IC3.Y1, IC7.2J
  !IN-A: U1.6Y, IC7.1K
  IN-A: U1.6A, IC3.Y2, IC7.1J
  5V: U1.VCC, IC3.VCC, IC6.1̅P̅R̅E̅, IC6.VCC, IC6.2P̅R̅E̅, IC7.1̅P̅R̅E̅, IC7.VCC, IC7.2P̅R̅E̅, IC8.OUT, C2_0_1uF.+, R1.Pin_0, U2.Reset, U2.Vcc_Supply_Voltage, R6.Pin_1, R7.Pin_1, S4.L1
  OUT-A: IC3.A1, IC7.1Q, LED1.anode
  OUT-D: IC3.B1, IC3.B2, IC3.A3, IC3.A4, IC6.2Q, LED4.anode
  OUT-Z: IC3.A2, S4.COM
  OUT-C: IC3.B3, IC6.1Q, LED3.anode
  OUT-B: IC3.B4, IC7.2Q, LED2.anode
  clock: IC6.1CLK, IC6.2CLK, IC7.1CLK, IC7.2CLK, U2.Output
  CLR: IC6.1̅C̅L̅R̅, IC6.2C̅L̅R̅, IC7.1̅C̅L̅R̅, IC7.2C̅L̅R̅, S1.1, S1.2, R1.Pin_1
  N1: IC8.IN, C1_0_33uF.+, S2.L2
  N2: J1.pin2, S2.COM
  N3: LED1.cathode, R5.Pin_0
  N4: LED2.cathode, R4.Pin_0
  N5: LED3.cathode, R3.Pin_0
  N6: LED4.cathode, R2.Pin_0
  N7: U2.Trigger, R7.Pin_0, S3.1, S3.2
  N8: U2.Control_Voltage, C2.+
  N9: U2.Threshold, U2.Discharge, R6.Pin_0, C1.+

notes:
  Clock generator
  voltage regurator
  reset
  clock
  on/off
  Bit 0
  Bit 1
  Bit 2
  Bit 3
  data
  X^0
  X^1
  X^2
  X^3

custom parts:
  DIP - 14 pins: A DIP stand-in part for whatever IC you want. With 14 pins on a 300mil dual inline package (DIP) footprint.
  DIP - 16 pins: A DIP stand-in part for whatever IC you want. With 16 pins on a 300mil dual inline package (DIP) footprint.
  Momentary Switch: Momentary Switch Button commonly used for reset or general input. Spark Fun Electronics SKU : COM-00097
